# Fritzing sketch clock (saved by Fritzing 1.0.3b)
breadboards: 1

parts:
  Part1 = Arduino Pro Mini (3.3V)
  8x8_LED_Modul_mit_MAX1 = 8x8 LED Modul mit MAX7219
  S2 = Pushbutton [package="[SMD]"]
  S3 = Pushbutton [package="[SMD]"]
  S4 = Pushbutton [package="[SMD]"]
  R1 = Rotary Potentiometer (Small) [maximum_resistance=100kΩ knob_status=50% power=0.5W package=THT]
  DS1 = DS18B20 1-Wire Temperature Sensor [part_number=DS18B20]
  R2 = Resistor [tolerance=±5% power=0.25W resistance=220 package=THT]
  IC1 = DS1302 [package="DIP8 [THT]"]
  BAT1 = Battery Holders [package=battcom_20mm_pth]
  XTAL1 = Crystal [frequency="16 Mhz" package=SMD]

nets:
  GND: Part1.GND, 8x8_LED_Modul_mit_MAX1.connector0, 8x8_LED_Modul_mit_MAX1.connector1, R1.leg2, DS1.GND, IC1.0V, IC1.Vbat_-_Backup_Supply, BAT1.-
  VCC: Part1.VCC, S2.Pin_3, S2.Pin_4, S3.Pin_3, S3.Pin_4, S4.Pin_3, S4.Pin_4, R1.leg1, DS1.VDD, R2.Pin_0
  N1: S2.Pin_1, S2.Pin_2
  N2: S3.Pin_1, S3.Pin_2
  N3: S4.Pin_1, S4.Pin_2
  N4: DS1.DQ, R2.Pin_1
  N5: IC1.+V, BAT1.+
  N6: IC1.X1_-_Crystal, XTAL1.pin_1
  N7: IC1.X2_-_Crystal, XTAL1.pin_0
